# Fritzing sketch prueba de insolado (saved by Fritzing 0.8.7b)
circuit board: 6.79608cm x 2.65288cm

parts:
  5_min = mystery part, 6 pins [chip_label=?]
  4_min = mystery part, 6 pins [chip_label=?]
  3_min = mystery part, 6 pins [chip_label=?]
  2_min = mystery part, 6 pins [chip_label=?]
  1_min = mystery part, 6 pins [chip_label=?]

nets:
  N1: 5_min.pin1, 4_min.pin1, 3_min.pin1, 2_min.pin1, 1_min.pin1
  N2: 5_min.pin2, 4_min.pin2, 3_min.pin2, 2_min.pin2, 1_min.pin2
  N3: 5_min.pin3, 4_min.pin3, 3_min.pin3, 2_min.pin3, 1_min.pin3
  N4: 5_min.pin4, 4_min.pin4, 3_min.pin4, 2_min.pin4, 1_min.pin4
  N5: 5_min.pin5, 4_min.pin5, 3_min.pin5, 2_min.pin5, 1_min.pin5
  N6: 5_min.pin6, 4_min.pin6, 3_min.pin6, 2_min.pin6, 1_min.pin6

notes:
  Prueba de insolado
  5 min
  4 min
  3 min
  2 min
  1 min
