# Fritzing sketch temporizador_insoladora_attiny85 (saved by Fritzing 0.8.7b)
circuit board: 4.96523cm x 2.86255cm

parts:
  Attiny85 = ATTINY45 [package=dip]
  LED1 = LED - 5mm [color="Red (633nm)" package="5 mm [THT]"]
  LED2 = LED - 5mm [color="Red (633nm)" package="5 mm [THT]"]
  470 = Resistor [tolerance=±5% resistance=470 package=THT]
  470_2 = Resistor [tolerance=±5% resistance=470 package=THT]
  LED_4 = LED - 5mm [color="Infrared (850nm)" package="5 mm [THT]"]
  10k = Resistor [tolerance=±5% resistance=10k package=THT]
  BD137 = NPN-Transistor [package="TO92 [THT]"]
  Vin = Screw terminal - 2 pins [package=THT]
  P1 = Pushbutton [package=THT]
  P2 = Pushbutton [package=THT]
  10k_2 = Resistor [tolerance=±5% resistance=10k package=THT]
  10K = Resistor [tolerance=±5% resistance=10k package=THT]
  LED_3 = LED - 5mm [color="Green (570nm)" package="5 mm [THT]"]
  470_3 = Resistor [tolerance=±5% resistance=470 package=THT]
  7805 = Voltage Regulator - 5V [package="TO220 [THT]"]
  470uF/16v = Electrolytic Capacitor [capacitance=47µF package="100 mil [THT, electrolytic]"]
  1K = Resistor [tolerance=±5% resistance=1k package=THT]
  Salida = Screw terminal - 2 pins [package=THT]

nets:
  N1: Attiny85.PB3(ADC3), 10k.Pin_1
  N2: Attiny85.PB4(ADC2), P2.leg1, 10K.Pin_0
  GND: Attiny85.GND, LED1.cathode, LED2.cathode, BD137.E, Vin.pin1, P1.leg0, P2.leg0, LED_3.cathode, 7805.GND, 470uF/16v.-
  N3: Attiny85.PB0(MOSI), 470.Pin_1
  N4: Attiny85.PB1(MISO), 470_2.Pin_1
  N5: Attiny85.PB2(SCK_ADC1), P1.leg1, 10k_2.Pin_0
  N6: Attiny85.VCC, 10k_2.Pin_1, 10K.Pin_1, 470_3.Pin_1, 7805.output_voltage, 470uF/16v.+
  N7: LED1.anode, 470.Pin_0
  N8: LED2.anode, 470_2.Pin_0
  N9: LED_4.cathode, BD137.C, Salida.pin2
  N10: LED_4.anode, 1K.Pin_1
  N11: 10k.Pin_0, BD137.B
  N12: Vin.pin2, 7805.input_voltage, 1K.Pin_0, Salida.pin1
  N13: LED_3.anode, 470_3.Pin_0

notes:
  PLACA LED IR
  BD137
  E  C  B
  LED 2
  LED 1
  LED 3
  10K
  470
  Attiny85
  7805
  Pulsador 1
  Pulsador 2
  LED 1  OFF - LED 2  OFF - 100Seg
  LED 1  ON  -  LED 2  OFF - 120Seg
  LED 1  OFF -  LED 2  ON - 140Seg
  LED 1  ON  -  LED 2  ON - 160Seg
  Subir Tiempo
  Empezar
  Temporizador
  470uF
  16V
  LED 4
  1K
  +
  -
  b
  c
  e
